# Fritzing sketch MoonlightFocuser (saved by Fritzing 0.9.3b)

parts:
  Board = Arduino Uno (Rev3)
  TEMPSENSOR = DS18B20 1-Wire Temperature Sensor [part_number=DS18B20]
  R1 = Resistor [tolerance=±5% resistance=4.7k package="0603 [SMD]"]
  C1 = Electrolytic Capacitor [capacitance=0.47mF voltage=16V package="100 mil [THT, electrolytic]"]
  Display = OLED 128x64 I2C Monochrome Display
  MOMENTARY_SWITCH_-_SPEED_(D12) = SWITCH-MOMENTARY-2 [package=tactile-pth]
  MOMENTARY_SWITCH_-_BACKWARD_(D11) = SWITCH-MOMENTARY-2 [package=tactile-pth]
  MOMENTARY_SWITCH_-_FORWARD_(D10) = SWITCH-MOMENTARY-2 [package=tactile-pth]
  R2 = Resistor [tolerance=±5% resistance=10k package="2512 [SMD]"]
  R3 = Resistor [tolerance=±5% resistance=10k package="1206 [SMD]"]
  R4 = Resistor [tolerance=±5% resistance=10k package="1206 [SMD]"]
  SM2 = 28BYJ-48 Stepper Motor [part_number=28BYJ-48]
  DRIVER = 28BYJ-48 Driver Module [part_number=ULN2003 package=THT]
  SWITCH_C1_(UPGRADE-RUN) = SWITCH-SPST-2 [package=switch-spst-vertical]
  MOMENTARY_SWITCH_-_DISPLAY_(D9) = SWITCH-MOMENTARY-2 [package=tactile-pth]
  R5 = Resistor [tolerance=±5% resistance=10k package="2512 [SMD]"]

nets:
  N1: Board.A4/SDA, Display.SDA
  N2: Board.A5/SCL, Display.SCK
  N3: Board.D9_PWM, MOMENTARY_SWITCH_-_DISPLAY_(D9).2, R5.Pin_0
  N4: Board.D10_PWM/SS, MOMENTARY_SWITCH_-_FORWARD_(D10).2, R4.Pin_0
  N5: Board.D11_PWM/MOSI, MOMENTARY_SWITCH_-_BACKWARD_(D11).2, R3.Pin_0
  N6: Board.D12/MISO, MOMENTARY_SWITCH_-_SPEED_(D12).2, R2.Pin_0
  GND: Board.GND, TEMPSENSOR.GND, Display.GND, R2.Pin_1, R3.Pin_1, R4.Pin_1, DRIVER.GND
  N7: Board.D2, TEMPSENSOR.DQ, R1.Pin_0
  N8: Board.D4, DRIVER.IN4
  N9: Board.D5_PWM, DRIVER.IN3
  N10: Board.D6_PWM, DRIVER.IN2
  N11: Board.D7, DRIVER.IN1
  N12: Board.RESET, C1.+
  VDD: Board.5V, TEMPSENSOR.VDD, Display.VDD, MOMENTARY_SWITCH_-_BACKWARD_(D11).1, MOMENTARY_SWITCH_-_FORWARD_(D10).1
  N13: R1.Pin_1, MOMENTARY_SWITCH_-_SPEED_(D12).1
  N14: C1.-, SWITCH_C1_(UPGRADE-RUN).O
  N15: SM2.blue-pin, DRIVER.blue-pin
  N16: SM2.pink-pin, DRIVER.pink-pin
  N17: SM2.yellow-pin, DRIVER.yellow-pin
  N18: SM2.orange-pin, DRIVER.orange-pin
  N19: SM2.red-pin, DRIVER.red-pin
  N20: DRIVER.Vmotor, MOMENTARY_SWITCH_-_DISPLAY_(D9).1
  N21: SWITCH_C1_(UPGRADE-RUN).P, R5.Pin_1

custom parts:
  28BYJ-48 Stepper Motor: Unipolar Stepper Motor 28BYJ-48 Top coil - pink & orange Bottom coil - blue & yellow Common rail - red Connector pins: blue - pink - yellow - orange - red
  28BYJ-48 Driver Module: Generic male header
